// Logisim project control.circ as structural Verilog: 1 circuit, main circuit main
module main (
  input  Start,
  input  Reset,
  input  lt,
  input  eq,
  input  prod0,
  input  Clk,
  output Lm,
  output Lmd,
  output Lp,
  output Sadd,
  output Sm,
  output Sp,
  output Count,
  output Clear,
  output Lr,
  output Shift
);

  wire and_2_out, and_4_out, and_8_out, and_9_out, and_10_out, and_11_out, and_12_out, and_13_out,
       and_14_out, and_15_out, and_16_out, and_17_out, and_18_out, and_19_out, and_20_out, and_21_out,
       and_22_out, and_23_out, not_1_out, not_2_out, not_3_out, not_4_out, not_5_out, not_6_out, not_7_out,
       not_8_out;
  wire [2:0] or_1_out, State_q;

  not not_1 (not_1_out, Start);
  not not_2 (not_2_out, Reset);
  not not_3 (not_3_out, lt);
  not not_4 (not_4_out, eq);
  not not_5 (not_5_out, prod0);
  Register #(.width(3)) State (.D(or_1_out), .en(1'b1), .Q(State_q), .clk(Clk));  // open: clr
  not not_6 (not_6_out, State_q[2]);
  not not_7 (not_7_out, State_q[0]);
  not not_8 (not_8_out, State_q[1]);
  and and_1 (Lmd, not_6_out, not_8_out, State_q[0]);
  and and_2 (and_2_out, not_6_out, State_q[1], not_7_out);
  and and_3 (Sadd, not_6_out, State_q[1], State_q[0]);
  and and_4 (and_4_out, State_q[2], not_8_out, not_7_out);
  and and_5 (Sm, State_q[2], not_8_out, State_q[0]);
  and and_6 (Count, State_q[2], State_q[1], not_7_out);
  and and_7 (Clear, State_q[2], State_q[1], State_q[0]);
  and and_8 (and_8_out, not_6_out, State_q[1], not_7_out, not_5_out);
  and and_9 (and_9_out, not_6_out, State_q[1], State_q[0]);
  and and_10 (and_10_out, State_q[2], not_8_out);
  and and_11 (and_11_out, State_q[2], State_q[1], not_7_out, eq);
  and and_12 (and_12_out, State_q[2], State_q[1], State_q[0], not_2_out);
  and and_13 (and_13_out, not_6_out, not_8_out, State_q[0]);
  and and_14 (and_14_out, not_6_out, State_q[1], not_7_out, prod0);
  and and_15 (and_15_out, State_q[2], not_8_out, State_q[0]);
  and and_16 (and_16_out, State_q[2], State_q[1], not_7_out, lt);
  and and_17 (and_17_out, State_q[2], State_q[1], not_7_out, eq);
  and and_18 (and_18_out, State_q[2], State_q[1], State_q[0], not_2_out);
  and and_19 (and_19_out, not_6_out, not_8_out, not_7_out, Start);
  and and_20 (and_20_out, not_6_out, State_q[1], not_7_out, prod0);
  or or_1 (or_1_out[0], and_19_out, and_20_out, and_21_out, and_22_out, and_23_out);
  and and_21 (and_21_out, State_q[2], not_8_out, not_7_out);
  and and_22 (and_22_out, State_q[2], State_q[1], not_7_out, eq);
  and and_23 (and_23_out, State_q[2], State_q[1], State_q[0], not_2_out);
  or or_2 (or_1_out[2], and_8_out, and_9_out, and_10_out, and_11_out, and_12_out);
  or or_3 (or_1_out[1], and_13_out, and_14_out, and_15_out, and_16_out, and_17_out, and_18_out);
  or or_4 (Lm, Lmd, Sm);
  or or_5 (Lp, Lmd, Sadd, and_4_out);
  or or_6 (Sp, Sadd, and_4_out);
  or or_7 (Shift, and_4_out, Sm);

  assign Lr = Clear;

  // Notes on the sheet:
  //   S1
  //   S2
  //   S3
  //   S4
  //   S5
  //   S6
  //   S7
  //   N2
  //   N1
  //   N0
endmodule
