// Logisim project datapath.circ as structural Verilog: 1 circuit, main circuit main
module main (
  input  Lm,
  input  Lmd,
  input  Lp,
  input  Sadd,
  input  Sm,
  input  Sp,
  input  Count,
  input  Clear,
  input  Lr,
  input  Shift,
  input  Clock,
  input  [31:0] Multiplicand,
  input  [31:0] Multipler,
  output gt,
  output eq,
  output lt,
  output prod0,
  output [31:0] Result_64_32,
  output [31:0] Result_31_0,
  output [4:0] Counter
);

  wire [31:0] adder_1_out, demultiplexer_1_out0, demultiplexer_1_out1, md_q, multiplexer_1_out,
       multiplexer_2_out, multiplexer_3_out, multiplexer_4_out, p_q, shifter_1_out;
  wire [31:1] m_q;
  wire [31:31] demultiplexer_1_out1_2;

  Multiplexer #(.width(32)) multiplexer_1 (
    .in0(Multipler), .in1(demultiplexer_1_out1), .out(multiplexer_1_out), .sel(Sm));  // open: en
  Register #(.width(32)) md (.D(Multiplicand), .en(Lmd), .Q(md_q), .clk(Clock));  // open: clr
  Multiplexer #(.width(32)) multiplexer_2 (
    .in0({32{1'b0}}), .in1(multiplexer_3_out), .out(multiplexer_2_out), .sel(Sp));  // open: en
  Multiplexer #(.width(32)) multiplexer_3 (
    .in0(demultiplexer_1_out0), .in1(adder_1_out), .out(multiplexer_3_out), .sel(Sadd));  // open: en
  Register #(.width(32)) m (.D(multiplexer_1_out), .en(Lm), .Q({m_q, prod0}), .clk(Clock));  // open: clr
  Adder #(.width(32)) adder_1 (.a(md_q), .b(p_q), .out(adder_1_out));  // open: cin, cout
  Register #(.width(32)) p (.D(multiplexer_2_out), .en(Lp), .Q(p_q), .clk(Clock));  // open: clr
  Multiplexer #(.width(32)) multiplexer_4 (
    .in0(p_q), .in1({m_q, prod0}), .out(multiplexer_4_out), .sel(Sm));  // open: en
  Demultiplexer #(.width(32)) demultiplexer_1 (
    .out0(demultiplexer_1_out0), .out1({demultiplexer_1_out1_2[31], demultiplexer_1_out1[30:0]}),
    .in(shifter_1_out), .sel(Sm));  // open: en
  Shifter #(.width(32), .shift("lr")) shifter_1 (
    .in(multiplexer_4_out), .\dist ({4'b0000, Shift}), .out(shifter_1_out));
  Counter #(.width(5), .max('h1f)) u_Counter (
    .count(Count), .Q(Counter), .clk(Clock), .clr(Clear));  // open: load, D, carry
  Register #(.width(1)) shifted (.D(p_q[0]), .en(Lp), .Q(demultiplexer_1_out1[31]), .clk(Clock));  // open: clr
  Register #(.width(32)) Result (.D(p_q), .en(Lr), .Q(Result_64_32), .clk(Clock));  // open: clr
  Register #(.width(32)) Result_2 (.D({m_q, prod0}), .en(Lr), .Q(Result_31_0), .clk(Clock));  // open: clr
  Comparator #(.width(5), .mode("unsigned")) comparator_1 (.a(Counter), .b({5{1'b1}}), .gt(gt), .eq(eq), .lt(lt));

  // Notes on the sheet:
  //   Product
endmodule
