// Logisim project mult32.circ as structural Verilog: 1 circuit, main circuit main
module main (
  input  [31:0] Multiplicand,
  input  [31:0] Multiplier,
  input  Start,
  output [31:0] Result_64_32,
  output [31:0] Result_31_0,
  output [4:0] Counter
);

  wire Clk_out, main_1_clear, main_1_count, main_1_lm, main_1_lmd, main_1_lp, main_1_lr, main_1_sadd,
       main_1_shift, main_1_sm, main_1_sp, main_2_eq, main_2_lt, main_2_prod0, Reset_out;

  Button Reset (.out(Reset_out));
  Clock Clk (.out(Clk_out));
  control_main main_1 (
    .Start(Start), .Reset(Reset_out), .lt(main_2_lt), .eq(main_2_eq), .prod0(main_2_prod0), .Clk(Clk_out),
    .Lm(main_1_lm), .Lmd(main_1_lmd), .Lp(main_1_lp), .Sadd(main_1_sadd), .Sm(main_1_sm), .Sp(main_1_sp),
    .Count(main_1_count), .Clear(main_1_clear), .Lr(main_1_lr), .Shift(main_1_shift));
  datapath_main main_2 (
    .Lm(main_1_lm), .Lmd(main_1_lmd), .Lp(main_1_lp), .Sadd(main_1_sadd), .Sm(main_1_sm), .Sp(main_1_sp),
    .Count(main_1_count), .Clear(main_1_clear), .Lr(main_1_lr), .Shift(main_1_shift), .Clock(Clk_out),
    .Multiplicand(Multiplicand), .Multipler(Multiplier), .eq(main_2_eq), .lt(main_2_lt),
    .prod0(main_2_prod0), .Result_64_32(Result_64_32), .Result_31_0(Result_31_0), .Counter(Counter));  // open: gt
endmodule
